# Fritzing sketch light-intensity-fritzing (saved by Fritzing 0.9.3b)
breadboards: 4

parts:
  Part1 = Arduino Nano (Rev3.0)
  LED1 = smd LED [color="Red (633nm)" package="0805 [SMD]"]
  LED2 = smd LED [color="Red (633nm)" package="0805 [SMD]"]
  LED3 = smd LED [color="Red (633nm)" package="0805 [SMD]"]
  R1 = Resistor [tolerance=±5% resistance=220 package="0402 [SMD]"]
  R2 = Resistor [tolerance=±5% resistance=220 package="0402 [SMD]"]
  R3 = Resistor [tolerance=±5% resistance=220 package="0402 [SMD]"]
  R4 = Resistor [tolerance=±5% resistance=220 package="0402 [SMD]"]
  R5 = Resistor [tolerance=±5% resistance=220 package="0402 [SMD]"]
  R6 = Photocell (LDR) [package=THT]
  J1 = Piezo Speaker
  LED4 = smd LED [color="Red (633nm)" package="0805 [SMD]"]
  LED5 = smd LED [color="Red (633nm)" package="0805 [SMD]"]
  LED6 = smd LED [color="Red (633nm)" package="0805 [SMD]"]
  R7 = Resistor [tolerance=±5% resistance=220 package="0402 [SMD]"]
  R8 = Resistor [tolerance=±5% resistance=220 package="0402 [SMD]"]
  R9 = Resistor [tolerance=±5% resistance=220 package="0402 [SMD]"]
  R10 = Resistor [tolerance=±5% resistance=220 package="0402 [SMD]"]
  R11 = Photocell (LDR) [package=THT]
  LED7 = smd LED [color="Red (633nm)" package="0805 [SMD]"]
  LED8 = smd LED [color="Red (633nm)" package="0805 [SMD]"]
  LED9 = smd LED [color="Red (633nm)" package="0805 [SMD]"]
  R12 = Resistor [tolerance=±5% resistance=220 package="0402 [SMD]"]
  R13 = Resistor [tolerance=±5% resistance=220 package="0402 [SMD]"]
  R14 = Resistor [tolerance=±5% resistance=220 package="0402 [SMD]"]
  R15 = Resistor [tolerance=±5% resistance=220 package="0402 [SMD]"]
  R16 = Photocell (LDR) [package=THT]

nets:
  N1: Part1.GND, R1.Pin_1, R4.Pin_0, R7.Pin_0, R8.Pin_0, R9.Pin_0, R10.Pin_0, R12.Pin_1, R13.Pin_1, R14.Pin_1, R15.Pin_1
  N2: Part1.D2, LED1.cathode
  N3: Part1.D3, LED2.cathode
  N4: Part1.D4, LED3.cathode
  N5: Part1.D5, LED7.cathode
  N6: Part1.D6, LED8.cathode
  N7: Part1.D7, LED9.cathode
  N8: Part1.D8, LED4.cathode
  N9: Part1.D9, LED5.cathode
  N10: Part1.D10, LED6.cathode
  N11: Part1.D11/MOSI, J1.pin1
  N12: Part1.5V, R6.pin_0, R11.pin_0, R16.pin_0
  N13: Part1.A3, R10.Pin_1
  N14: Part1.A2, R15.Pin_0
  N15: Part1.A1, R5.Pin_1
  N16: LED1.anode, R1.Pin_0
  N17: LED2.anode, R2.Pin_0
  N18: LED3.anode, R3.Pin_0
  N19: R2.Pin_1, R3.Pin_1, R5.Pin_0
  N20: LED4.anode, R7.Pin_1
  N21: LED5.anode, R8.Pin_1
  N22: LED6.anode, R9.Pin_1
  N23: LED7.anode, R12.Pin_0
  N24: LED8.anode, R13.Pin_0
  N25: LED9.anode, R14.Pin_0
